// Logisim project 16bitcpu.circ as structural Verilog
module main (
  input  reset,
  input  output_enable_enable,
  input  write_enable_enable,
  input  [2:0] outputRegRamALU,
  input  [2:0] write_enable_reg,
  input  [3:0] opcode,
  output [15:0] out_7,
  output [15:0] out_8,
  output [15:0] out_9,
  output [15:0] out_10,
  output [15:0] out_11,
  output Greater_A,
  output Smaller_A,
  output [15:0] out_14,
  output z_flag,
  output [15:0] out_16,
  output c_flag,
  output [15:0] out_18
);

  wire and_1_out, and_3_out, clock_1_out, demultiplexer_1_out0, demultiplexer_1_out1, demultiplexer_1_out3,
       demultiplexer_2_out0, demultiplexer_2_out1, demultiplexer_2_out2, demultiplexer_2_out3,
       demultiplexer_2_out4, demultiplexer_2_out5, demultiplexer_2_out6, demultiplexer_3_out0,
       demultiplexer_3_out1, demultiplexer_3_out2, demultiplexer_3_out3, demultiplexer_3_out4,
       demultiplexer_5_out0, demultiplexer_5_out1, demultiplexer_5_out2, demultiplexer_5_out3,
       multiplexer_4_out, multiplexer_7_out, not_1_out, or_1_out, or_2_out, or_4_out, or_5_out, or_6_out,
       or_7_out, or_8_out, or_9_out, or_10_out, or_11_out, or_12_out, or_13_out, or_14_out, or_15_out,
       or_16_out, or_17_out, or_18_out, pull_resistor_1_node;
  wire [2:0] multiplexer_3_out, multiplexer_5_out, pull_resistor_2_node, pull_resistor_3_node;
  wire [2:2] pull_resistor_5_node, pull_resistor_6_node;
  wire [3:0] output_register_out_5, output_register_out_5_2, output_register_out_5_3, output_register_out_5_4;
  wire [11:0] demultiplexer_4_out2, multiplexer_8_out, pull_resistor_7_node;
  wire [13:0] demultiplexer_4_out0, demultiplexer_4_out1, demultiplexer_4_out3;
  wire [13:12] demultiplexer_4_out2_2;
  wire [15:0] adder_1_out, and_2_out, divider_1_out, multiplier_1_out, not_2_out, or_3_out,
       pull_resistor_4_node, subtractor_1_out, xor_1_out;

  and and_1 (and_1_out, clock_1_out, not_1_out);
  Clock clock_1 (.out(clock_1_out));
  not not_1 (not_1_out, multiplexer_4_out);
  Hex_Digit_Display hex_digit_display_1 (.value(output_register_out_5_4));  // open: dp
  Hex_Digit_Display hex_digit_display_2 (.value(output_register_out_5_3));  // open: dp
  Hex_Digit_Display hex_digit_display_3 (.value(output_register_out_5_2));  // open: dp
  Hex_Digit_Display hex_digit_display_4 (.value(output_register_out_5));  // open: dp
  BitSelector bitselector_1 ();  // open: in, out, sel
  // Probe on {output_register_out_5_4, output_register_out_5_3, output_register_out_5_2, output_register_out_5}
  Demultiplexer #(.select(2)) demultiplexer_1 (
    .out0(demultiplexer_1_out0), .out1(demultiplexer_1_out1), .out3(demultiplexer_1_out3), .in(1'b1),
    .sel(out_10[15:14]));  // open: out2
  or or_1 (or_1_out, demultiplexer_1_out0, demultiplexer_1_out1);
  or or_2 (or_2_out, demultiplexer_1_out0, demultiplexer_1_out3);
  registers r0 (
    .data_in(out_7), .write_enable(demultiplexer_2_out0), .clk_in(and_1_out),
    .read_enable(demultiplexer_3_out0), .out_5(out_7));
  registers r1 (
    .data_in(out_7), .write_enable(demultiplexer_2_out1), .clk_in(and_1_out),
    .read_enable(demultiplexer_3_out1), .out_5(out_7));
  registers r2 (
    .data_in(out_7), .write_enable(demultiplexer_2_out2), .clk_in(and_1_out),
    .read_enable(demultiplexer_3_out2), .out_5(out_7));
  registers r3 (
    .data_in(out_7), .write_enable(demultiplexer_2_out3), .clk_in(and_1_out),
    .read_enable(demultiplexer_3_out3), .out_5(out_7));
  registers rA (
    .data_in(out_7), .write_enable(demultiplexer_2_out4), .clk_in(and_1_out), .read_enable(1'b1),
    .out_5(out_11));
  registers rB (
    .data_in(out_7), .write_enable(demultiplexer_2_out5), .clk_in(and_1_out), .read_enable(1'b1),
    .out_5(out_14));
  registers output_register (
    .data_in(out_7), .write_enable(demultiplexer_2_out6), .clk_in(and_1_out), .read_enable(1'b1),
    .out_5({output_register_out_5_4, output_register_out_5_3, output_register_out_5_2, output_register_out_5}));
  Demultiplexer #(.select(3)) demultiplexer_2 (
    .out0(demultiplexer_2_out0), .out1(demultiplexer_2_out1), .out2(demultiplexer_2_out2),
    .out3(demultiplexer_2_out3), .out4(demultiplexer_2_out4), .out5(demultiplexer_2_out5),
    .out6(demultiplexer_2_out6), .in(or_2_out), .sel(multiplexer_3_out));  // open: out7
  Demultiplexer #(.select(3)) demultiplexer_3 (
    .out0(demultiplexer_3_out0), .out1(demultiplexer_3_out1), .out2(demultiplexer_3_out2),
    .out3(demultiplexer_3_out3), .out4(demultiplexer_3_out4), .in(or_1_out), .sel(multiplexer_5_out));  // open: out5, out6, out7
  Multiplexer #(.width(16)) multiplexer_1 (.in1(out_16), .out(out_7), .sel(demultiplexer_3_out4));  // open: in0
  Multiplexer #(.width(16)) multiplexer_2 (.in1(out_9), .out(out_7), .sel(demultiplexer_5_out3));  // open: in0
  Pull_Resistor pull_resistor_1 (.node(pull_resistor_1_node));
  Multiplexer #(.select(2), .width(3)) multiplexer_3 (
    .in0(demultiplexer_4_out0[6:4]), .in1(pull_resistor_2_node), .in2(pull_resistor_2_node),
    .in3({pull_resistor_5_node[2], demultiplexer_4_out3[13:12]}), .out(multiplexer_3_out), .sel(out_10[15:14]));
  program_counter program_counter_1 (
    .data_bus(demultiplexer_4_out2), .load_bus1_add1_0(and_3_out), .resetpc(reset), .clockkk(and_1_out),
    .write_enable(1'b1), .ooutt(out_8));
  Pull_Resistor pull_resistor_2 (.node(pull_resistor_2_node));
  Multiplexer #(.select(4)) multiplexer_4 (
    .in0(pull_resistor_1_node), .in1(pull_resistor_1_node), .in2(pull_resistor_1_node),
    .in3(pull_resistor_1_node), .in4(pull_resistor_1_node), .in5(pull_resistor_1_node),
    .in6(pull_resistor_1_node), .in7(pull_resistor_1_node), .in8(pull_resistor_1_node),
    .in9(pull_resistor_1_node), .in10(pull_resistor_1_node), .in11(pull_resistor_1_node),
    .in12(pull_resistor_1_node), .in13(pull_resistor_1_node), .in14(pull_resistor_1_node), .in15(1'b1),
    .out(multiplexer_4_out), .sel(demultiplexer_4_out0[13:10]));
  Demultiplexer #(.select(2), .width(14)) demultiplexer_4 (
    .out0(demultiplexer_4_out0), .out1(demultiplexer_4_out1),
    .out2({demultiplexer_4_out2_2, demultiplexer_4_out2}), .out3(demultiplexer_4_out3), .in(out_10[13:0]),
    .sel(out_10[15:14]));
  Demultiplexer #(.select(2)) demultiplexer_5 (
    .out0(demultiplexer_5_out0), .out1(demultiplexer_5_out1), .out2(demultiplexer_5_out2),
    .out3(demultiplexer_5_out3), .in(1'b1), .sel(out_10[15:14]));
  Adder #(.width(16)) adder_1 (.a(out_11), .b(out_14), .out(adder_1_out), .cout(c_flag));  // open: cin
  Subtractor #(.width(16)) subtractor_1 (.a(out_11), .b(out_14), .out(subtractor_1_out));  // open: bin, bout
  Multiplier #(.width(16)) multiplier_1 (.a(out_11), .b(out_14), .out(multiplier_1_out));  // open: cin, cout
  Divider #(.width(16)) divider_1 (.a(out_11), .b(out_14), .out(divider_1_out));  // open: upper, rem
  assign not_2_out = ~out_11;  // NOT_Gate not_2, 16 bits wide
  assign and_2_out = out_11 & out_14;  // AND_Gate and_2, 16 bits wide
  assign or_3_out = out_11 | out_14;  // OR_Gate or_3, 16 bits wide
  assign xor_1_out = out_11 ^ out_14;  // XOR_Gate xor_1, 16 bits wide
  Comparator #(.mode("unsigned"), .width(16)) comparator_1 (
    .a(out_11), .b(out_14), .gt(Greater_A), .lt(Smaller_A));  // open: eq
  and and_3 (and_3_out, multiplexer_7_out, demultiplexer_5_out2);
  Multiplexer #(.select(2), .width(3)) multiplexer_5 (
    .in0(demultiplexer_4_out0[9:7]), .in1({pull_resistor_6_node[2], demultiplexer_4_out1[13:12]}),
    .in2(pull_resistor_3_node), .in3(pull_resistor_3_node), .out(multiplexer_5_out), .sel(out_10[15:14]));
  Pull_Resistor pull_resistor_3 (.node(pull_resistor_3_node));
  Pull_Resistor pull_resistor_4 (.node(pull_resistor_4_node));
  ROM #(.addrWidth(16), .dataWidth(16)) program_memory (.addr(out_8), .data(out_10));
  Multiplexer #(.select(4), .width(16)) multiplexer_6 (
    .in0(adder_1_out), .in1(subtractor_1_out), .in2(multiplier_1_out), .in3(divider_1_out), .in4(not_2_out),
    .in5(and_2_out), .in6(or_3_out), .in7(xor_1_out), .in8(out_11), .in9(out_14),
    .in10(pull_resistor_4_node), .in11(pull_resistor_4_node), .in12(pull_resistor_4_node),
    .in13(pull_resistor_4_node), .in14(pull_resistor_4_node), .in15(pull_resistor_4_node), .out(out_16),
    .sel(demultiplexer_4_out0[13:10]));
  Pull_Resistor pull_resistor_5 (.node(pull_resistor_5_node[2]));
  or or_4 (or_4_out, or_3_out[0], or_3_out[1]);
  or or_5 (or_5_out, or_3_out[2], or_3_out[3]);
  or or_6 (or_6_out, or_3_out[4], or_3_out[5]);
  or or_7 (or_7_out, or_3_out[6], or_3_out[7]);
  or or_8 (or_8_out, or_3_out[8], or_3_out[9]);
  or or_9 (or_9_out, or_3_out[10], or_3_out[11]);
  or or_10 (or_10_out, or_3_out[12], or_3_out[13]);
  or or_11 (or_11_out, or_3_out[14], or_3_out[15]);
  Pull_Resistor pull_resistor_6 (.node(pull_resistor_6_node[2]));
  RAM #(.addrWidth(12), .asyncread("true"), .dataWidth(16)) ram_1 (
    .addr(multiplexer_8_out), .we(demultiplexer_5_out1), .oe(demultiplexer_5_out3), .clk(and_1_out),
    .din(out_7), .dout(out_9));
  or or_12 (or_12_out, or_4_out, or_5_out);
  or or_13 (or_13_out, or_6_out, or_7_out);
  or or_14 (or_14_out, or_8_out, or_9_out);
  or or_15 (or_15_out, or_10_out, or_11_out);
  Multiplexer #(.select(2)) multiplexer_7 (
    .in0(z_flag), .in1(Greater_A), .in2(Smaller_A), .in3(c_flag), .out(multiplexer_7_out),
    .sel(demultiplexer_4_out2_2));
  or or_16 (or_16_out, or_12_out, or_13_out);
  or or_17 (or_17_out, or_14_out, or_15_out);
  or or_18 (or_18_out, or_16_out, or_17_out);
  Pull_Resistor pull_resistor_7 (.node(pull_resistor_7_node));
  not not_3 (z_flag, or_18_out);
  Multiplexer #(.select(2), .width(12)) multiplexer_8 (
    .in0(demultiplexer_4_out1[11:0]), .in1(pull_resistor_7_node), .in2(pull_resistor_7_node),
    .in3(demultiplexer_4_out3[11:0]), .out(multiplexer_8_out), .sel(out_10[15:14]));

  assign out_18 = out_10;

  // Notes on the sheet:
  //   WRITE ENABLE
  //   READ ENABLE
  //   Instr_reg0ram
  //   12 bits
  //   12bit to 16bit
  //   SIDDHCESNA - II
  //   TYPE
  //   LOGIC AND MATHS
  //   MEMORY JUMP
  //   src
  //   contents of program_memory (hex, n*v repeats v):
  //   c000 d001 2040 24d0 220 2560 2090 2110 8002
  //   opcode
  //   MEMORY ADDRESS
  //   JUMP FLAGS
  //   LDM
  //   STR
  //   MEMORY ADDRESS
  //   MEMORY ADDRESS
  //   REG_0-3
  //   FLAGS
  //   REG_0-3
  //   RAM IS IN TYPE 00 means it have read/write with other
endmodule

module mainn (
  input  manual_clk,
  input  [15:0] in_2,
  input  in_3,
  input  in_4,
  input  [15:0] in_5,
  input  in_6,
  input  w_enable_pc,
  input  read_enable_ALU_RAM,
  input  in_9,
  input  [3:0] opcode,
  input  in_11,
  input  [1:0] in_12,
  input  write_enable_ram,
  input  [15:0] in_14,
  output [15:0] out_15,
  output Z,
  output [15:0] outp,
  output C,
  output [1:0] out_19,
  output [1:0] out_20
);

  wire CLOCK_1_out, demultiplexer_1_out0, demultiplexer_1_out1, demultiplexer_2_out0, demultiplexer_2_out1,
       demultiplexer_2_out2, demultiplexer_2_out3, demultiplexer_3_out1, demultiplexer_4_out0,
       demultiplexer_4_out1, demultiplexer_4_out2, demultiplexer_4_out3, demultiplexer_5_out0,
       demultiplexer_5_out1, multiplexer_1_out, not_1_out, not_2_out, or_2_out, or_3_out, or_4_out, or_5_out,
       or_6_out, or_7_out, or_8_out, or_9_out, or_10_out, or_11_out, or_12_out, or_13_out, or_14_out,
       or_15_out, or_16_out;
  wire [1:0] adder_1_out, pull_resistor_2_node, pull_resistor_3_node;
  wire [3:0] demultiplexer_6_out0, demultiplexer_6_out1;
  wire [15:0] adder_2_out, and_1_out, divider_1_out, multiplier_1_out, not_3_out, or_1_out,
       program_counter_1_p5, pull_resistor_5_node, ram_1_dout, register_a_out_5, register_b_out_5,
       subtractor_1_out, xor_1_out;

  registers registers_1 (.data_in(in_2), .write_enable(in_3), .clk_in(manual_clk), .read_enable(in_4));  // open: out_5
  Pull_Resistor pull_resistor_1 (.node(in_2));
  Demultiplexer demultiplexer_1 (
    .out0(demultiplexer_1_out0), .out1(demultiplexer_1_out1), .in(read_enable_ALU_RAM), .sel(in_9));
  Multiplexer multiplexer_1 (.in0(demultiplexer_2_out0), .in1(not_1_out), .out(multiplexer_1_out), .sel(out_20[0]));
  not not_1 (not_1_out, demultiplexer_2_out1);
  Demultiplexer #(.select(2)) demultiplexer_2 (
    .out0(demultiplexer_2_out0), .out1(demultiplexer_2_out1), .out2(demultiplexer_2_out2),
    .out3(demultiplexer_2_out3), .in(1'b1), .sel(out_19));
  Demultiplexer #(.select(2)) demultiplexer_3 (
    .out1(demultiplexer_3_out1), .in(1'b1), .sel(out_20));  // open: out0, out2, out3
  Demultiplexer #(.select(2)) demultiplexer_4 (
    .out0(demultiplexer_4_out0), .out1(demultiplexer_4_out1), .out2(demultiplexer_4_out2),
    .out3(demultiplexer_4_out3), .in(in_11), .sel(in_12));
  Demultiplexer demultiplexer_5 (
    .out0(demultiplexer_5_out0), .out1(demultiplexer_5_out1), .in(demultiplexer_3_out1), .sel(not_2_out));
  not not_2 (not_2_out, multiplexer_1_out);
  Register #(.width(2)) register_1 (.D(adder_1_out), .en(1'b1), .clk(CLOCK_1_out), .Q(out_20));  // open: clr
  Adder #(.width(2)) adder_1 (.a(out_20), .b(2'b01), .out(adder_1_out));  // open: cin, cout
  main main_1 ();  // open: reset, output_enable_enable, write_enable_enable, outputRegRamALU, write_enable_reg, opcode, out_7, out_8, out_9, out_10, out_11, Greater_A, Smaller_A, out_14, z_flag, out_16, c_flag, out_18
  Clock CLOCK_1 (.out(CLOCK_1_out));
  Multiplexer #(.select(2), .width(2)) multiplexer_2 (
    .in0(in_14[10:9]), .in1(in_14[8:7]), .in2(pull_resistor_2_node), .in3(pull_resistor_3_node),
    .out(out_19), .sel(out_20));
  Pull_Resistor pull_resistor_2 (.node(pull_resistor_2_node));
  Pull_Resistor pull_resistor_3 (.node(pull_resistor_3_node));
  Demultiplexer #(.width(4)) demultiplexer_6 (
    .out0(demultiplexer_6_out0), .out1(demultiplexer_6_out1), .in(in_14[14:11]), .sel(in_14[15]));
  registers R_0 (
    .data_in(in_5), .write_enable(demultiplexer_4_out0), .clk_in(CLOCK_1_out),
    .read_enable(demultiplexer_2_out0), .out_5(in_5));
  registers R_1 (
    .data_in(in_5), .write_enable(demultiplexer_4_out1), .clk_in(CLOCK_1_out),
    .read_enable(demultiplexer_2_out1), .out_5(in_5));
  registers R_2 (
    .data_in(in_5), .write_enable(demultiplexer_4_out2), .clk_in(CLOCK_1_out),
    .read_enable(demultiplexer_2_out2), .out_5(in_5));
  registers R_3 (
    .data_in(in_5), .write_enable(demultiplexer_4_out3), .clk_in(CLOCK_1_out),
    .read_enable(demultiplexer_2_out3), .out_5(in_5));
  registers register_a (
    .data_in(in_5), .write_enable(demultiplexer_5_out0), .clk_in(CLOCK_1_out), .read_enable(1'b1),
    .out_5(register_a_out_5));
  registers register_b (
    .data_in(in_5), .write_enable(demultiplexer_5_out1), .clk_in(CLOCK_1_out), .read_enable(1'b1),
    .out_5(register_b_out_5));
  Pull_Resistor pull_resistor_4 (.node(in_5));
  Multiplexer #(.width(16)) multiplexer_3 (.in1(outp), .out(in_5), .sel(demultiplexer_1_out0));  // open: in0
  Multiplexer #(.width(16)) multiplexer_4 (.in1(ram_1_dout), .out(in_5), .sel(demultiplexer_1_out1));  // open: in0
  main main_2 ();  // open: reset, output_enable_enable, write_enable_enable, outputRegRamALU, write_enable_reg, opcode, out_7, out_8, out_9, out_10, out_11, Greater_A, Smaller_A, out_14, z_flag, out_16, c_flag, out_18
  // program_counter program_counter_1: pin names not known; wires that end beside it: in_5, in_6, CLOCK_1_out, w_enable_pc, program_counter_1_p5
  Adder #(.width(16)) adder_2 (.a(register_a_out_5), .b(register_b_out_5), .out(adder_2_out), .cout(C));  // open: cin
  Subtractor #(.width(16)) subtractor_1 (
    .a(register_a_out_5), .b(register_b_out_5), .out(subtractor_1_out));  // open: bin, bout
  Multiplier #(.width(16)) multiplier_1 (
    .a(register_a_out_5), .b(register_b_out_5), .out(multiplier_1_out));  // open: cin, cout
  Divider #(.width(16)) divider_1 (
    .a(register_a_out_5), .b(register_b_out_5), .out(divider_1_out));  // open: upper, rem
  assign not_3_out = ~register_a_out_5;  // NOT_Gate not_3, 16 bits wide
  assign and_1_out = register_a_out_5 & register_b_out_5;  // AND_Gate and_1, 16 bits wide
  assign or_1_out = register_a_out_5 | register_b_out_5;  // OR_Gate or_1, 16 bits wide
  assign xor_1_out = register_a_out_5 ^ register_b_out_5;  // XOR_Gate xor_1, 16 bits wide
  Pull_Resistor pull_resistor_5 (.node(pull_resistor_5_node));
  RAM #(.addrWidth(16), .dataWidth(16)) ram_1 (
    .addr(program_counter_1_p5), .we(write_enable_ram), .oe(1'b1), .clk(CLOCK_1_out), .din(in_5),
    .dout(ram_1_dout));
  Multiplexer #(.select(4), .width(16)) multiplexer_5 (
    .in0(adder_2_out), .in1(subtractor_1_out), .in2(multiplier_1_out), .in3(divider_1_out), .in4(not_3_out),
    .in5(and_1_out), .in6(or_1_out), .in7(xor_1_out), .in8(register_a_out_5), .in9(register_b_out_5),
    .in10(pull_resistor_5_node), .in11(pull_resistor_5_node), .in12(pull_resistor_5_node),
    .in13(pull_resistor_5_node), .in14(pull_resistor_5_node), .in15(pull_resistor_5_node), .out(outp),
    .sel(opcode));
  or or_2 (or_2_out, or_1_out[0], or_1_out[1]);
  or or_3 (or_3_out, or_1_out[2], or_1_out[3]);
  or or_4 (or_4_out, or_1_out[4], or_1_out[5]);
  or or_5 (or_5_out, or_1_out[6], or_1_out[7]);
  or or_6 (or_6_out, or_1_out[8], or_1_out[9]);
  or or_7 (or_7_out, or_1_out[10], or_1_out[11]);
  or or_8 (or_8_out, or_1_out[12], or_1_out[13]);
  or or_9 (or_9_out, or_1_out[14], or_1_out[15]);
  or or_10 (or_10_out, or_2_out, or_3_out);
  or or_11 (or_11_out, or_4_out, or_5_out);
  or or_12 (or_12_out, or_6_out, or_7_out);
  or or_13 (or_13_out, or_8_out, or_9_out);
  or or_14 (or_14_out, or_10_out, or_11_out);
  or or_15 (or_15_out, or_12_out, or_13_out);
  or or_16 (or_16_out, or_14_out, or_15_out);
  not not_4 (Z, or_16_out);

  assign out_15 = in_5;

  // Notes on the sheet:
  //   0 for w enable of A and B respectively
endmodule

module registers (
  input  [15:0] data_in,
  input  write_enable,
  input  clk_in,
  input  read_enable,
  output [15:0] out_5
);

  wire [15:0] register_1_q, undriven;

  Register #(.width(16)) register_1 (.D(data_in), .en(write_enable), .clk(clk_in), .Q(register_1_q));  // open: clr
  Multiplexer #(.width(16)) multiplexer_1 (.in0(undriven), .in1(register_1_q), .out(out_5), .sel(read_enable));
endmodule

module program_counter (
  input  [11:0] data_bus,
  input  load_bus1_add1_0,
  input  resetpc,
  input  clockkk,
  input  write_enable,
  output [15:0] ooutt
);

  wire and_1_out;
  wire [15:0] adder_1_out, multiplexer_1_out;
  wire [15:15] pull_resistor_1_node;

  Pull_Resistor pull_resistor_1 (.node(pull_resistor_1_node[15]));
  Multiplexer #(.width(16)) multiplexer_1 (
    .in0(adder_1_out), .in1({{4{pull_resistor_1_node[15]}}, data_bus}), .out(multiplexer_1_out),
    .sel(load_bus1_add1_0));
  and and_1 (and_1_out, clockkk, write_enable);
  D_Flip_Flop d_ff_1 (.D(multiplexer_1_out[15]), .clk(and_1_out), .Q(ooutt[15]), .reset(resetpc));  // open: Qn, preset
  D_Flip_Flop d_ff_2 (.D(multiplexer_1_out[14]), .clk(and_1_out), .Q(ooutt[14]), .reset(resetpc));  // open: Qn, preset
  D_Flip_Flop d_ff_3 (.D(multiplexer_1_out[13]), .clk(and_1_out), .Q(ooutt[13]), .reset(resetpc));  // open: Qn, preset
  D_Flip_Flop d_ff_4 (.D(multiplexer_1_out[12]), .clk(and_1_out), .Q(ooutt[12]), .reset(resetpc));  // open: Qn, preset
  D_Flip_Flop d_ff_5 (.D(multiplexer_1_out[11]), .clk(and_1_out), .Q(ooutt[11]), .reset(resetpc));  // open: Qn, preset
  D_Flip_Flop d_ff_6 (.D(multiplexer_1_out[10]), .clk(and_1_out), .Q(ooutt[10]), .reset(resetpc));  // open: Qn, preset
  D_Flip_Flop d_ff_7 (.D(multiplexer_1_out[9]), .clk(and_1_out), .Q(ooutt[9]), .reset(resetpc));  // open: Qn, preset
  D_Flip_Flop d_ff_8 (.D(multiplexer_1_out[8]), .clk(and_1_out), .Q(ooutt[8]), .reset(resetpc));  // open: Qn, preset
  D_Flip_Flop d_ff_9 (.D(multiplexer_1_out[7]), .clk(and_1_out), .Q(ooutt[7]), .reset(resetpc));  // open: Qn, preset
  D_Flip_Flop d_ff_10 (.D(multiplexer_1_out[6]), .clk(and_1_out), .Q(ooutt[6]), .reset(resetpc));  // open: Qn, preset
  D_Flip_Flop d_ff_11 (.D(multiplexer_1_out[5]), .clk(and_1_out), .Q(ooutt[5]), .reset(resetpc));  // open: Qn, preset
  D_Flip_Flop d_ff_12 (.D(multiplexer_1_out[4]), .clk(and_1_out), .Q(ooutt[4]), .reset(resetpc));  // open: Qn, preset
  Adder #(.width(16)) adder_1 (.a(ooutt), .b(16'h1), .out(adder_1_out));  // open: cin, cout
  D_Flip_Flop d_ff_13 (.D(multiplexer_1_out[3]), .clk(and_1_out), .Q(ooutt[3]), .reset(resetpc));  // open: Qn, preset
  D_Flip_Flop d_ff_14 (.D(multiplexer_1_out[2]), .clk(and_1_out), .Q(ooutt[2]), .reset(resetpc));  // open: Qn, preset
  D_Flip_Flop d_ff_15 (.D(multiplexer_1_out[1]), .clk(and_1_out), .Q(ooutt[1]), .reset(resetpc));  // open: Qn, preset
  D_Flip_Flop d_ff_16 (.D(multiplexer_1_out[0]), .clk(and_1_out), .Q(ooutt[0]), .reset(resetpc));  // open: Qn, preset
endmodule

module ALU (
  input  [15:0] A,
  input  [15:0] B,
  input  [3:0] opcode,
  output Z,
  output [15:0] outp,
  output C
);

  wire or_2_out, or_3_out, or_4_out, or_5_out, or_6_out, or_7_out, or_8_out, or_9_out, or_10_out, or_11_out,
       or_12_out, or_13_out, or_14_out, or_15_out, or_16_out;
  wire [15:0] adder_1_out, and_1_out, divider_1_out, multiplier_1_out, not_1_out, or_1_out,
       pull_resistor_1_node, subtractor_1_out, xor_1_out;

  Adder #(.width(16)) adder_1 (.a(A), .b(B), .out(adder_1_out), .cout(C));  // open: cin
  Subtractor #(.width(16)) subtractor_1 (.a(A), .b(B), .out(subtractor_1_out));  // open: bin, bout
  Multiplier #(.width(16)) multiplier_1 (.a(A), .b(B), .out(multiplier_1_out));  // open: cin, cout
  Divider #(.width(16)) divider_1 (.a(A), .b(B), .out(divider_1_out));  // open: upper, rem
  assign not_1_out = ~A;  // NOT_Gate not_1, 16 bits wide
  assign and_1_out = A & B;  // AND_Gate and_1, 16 bits wide
  assign or_1_out = A | B;  // OR_Gate or_1, 16 bits wide
  assign xor_1_out = A ^ B;  // XOR_Gate xor_1, 16 bits wide
  Pull_Resistor pull_resistor_1 (.node(pull_resistor_1_node));
  Multiplexer #(.select(4), .width(16)) multiplexer_1 (
    .in0(adder_1_out), .in1(subtractor_1_out), .in2(multiplier_1_out), .in3(divider_1_out), .in4(not_1_out),
    .in5(and_1_out), .in6(or_1_out), .in7(xor_1_out), .in8(A), .in9(B), .in10(pull_resistor_1_node),
    .in11(pull_resistor_1_node), .in12(pull_resistor_1_node), .in13(pull_resistor_1_node),
    .in14(pull_resistor_1_node), .in15(pull_resistor_1_node), .out(outp), .sel(opcode));
  or or_2 (or_2_out, or_1_out[0], or_1_out[1]);
  or or_3 (or_3_out, or_1_out[2], or_1_out[3]);
  or or_4 (or_4_out, or_1_out[4], or_1_out[5]);
  or or_5 (or_5_out, or_1_out[6], or_1_out[7]);
  or or_6 (or_6_out, or_1_out[8], or_1_out[9]);
  or or_7 (or_7_out, or_1_out[10], or_1_out[11]);
  or or_8 (or_8_out, or_1_out[12], or_1_out[13]);
  or or_9 (or_9_out, or_1_out[14], or_1_out[15]);
  or or_10 (or_10_out, or_2_out, or_3_out);
  or or_11 (or_11_out, or_4_out, or_5_out);
  or or_12 (or_12_out, or_6_out, or_7_out);
  or or_13 (or_13_out, or_8_out, or_9_out);
  or or_14 (or_14_out, or_10_out, or_11_out);
  or or_15 (or_15_out, or_12_out, or_13_out);
  or or_16 (or_16_out, or_14_out, or_15_out);
  not not_2 (Z, or_16_out);
endmodule

module control_unit (
  input  [15:0] in_1
);

  wire [3:0] demultiplexer_1_out0;

  Demultiplexer #(.width(4)) demultiplexer_1 (
    .out0(demultiplexer_1_out0), .in(in_1[14:11]), .sel(in_1[15]));  // open: out1
endmodule

module state_register (
  input  clckck,
  output [1:0] out_2
);

  wire [1:0] adder_1_out;

  Register #(.width(2)) register_1 (.D(adder_1_out), .en(1'b1), .clk(clckck), .Q(out_2));  // open: clr
  Adder #(.width(2)) adder_1 (.a(out_2), .b(2'b01), .out(adder_1_out));  // open: cin, cout
endmodule

module Intstruction_register (
  input  [15:0] data_bbuss,
  input  write_enabllllle,
  input  clockkkk,
  output [15:0] ir_out
);

  Register #(.width(16)) register_1 (.D(data_bbuss), .en(write_enabllllle), .clk(clockkkk), .Q(ir_out));  // open: clr
endmodule
